// Logisim project cpu.circ as structural Verilog: 5 circuits, main circuit main
module main (
);

  wire clock_1_out, Control_Unit_load_msb_lsb_r, Control_Unit_load_msb_r, Control_Unit_read_write_ram,
       Control_Unit_write_ram, counter_1_reset, not_1_out, not_2_out, or_1_out;
  wire [3:0] counter_1_output, R_q, R_q_2, Swapper_2_output_2, Swapper_output_1, Swapper_output_2;
  wire [7:0] ram_1_data, ram_2_data, Selector_output;

  Counter counter_1 (.Clock(clock_1_out), .Reset(counter_1_reset), .Output(counter_1_output));
  RAM #(.addrWidth(4)) ram_1 (.addr(counter_1_output), .data(ram_1_data), .sel(1'b1));  // open: clk, ld, clr
  Clock clock_1 (.out(clock_1_out));
  not not_1 (not_1_out, Control_Unit_load_msb_lsb_r);
  Control_Unit Control_Unit (
    .Input(ram_1_data[7:4]), .Load_msb_lsb_R(Control_Unit_load_msb_lsb_r),
    .Load_msb_R(Control_Unit_load_msb_r), .Write_RAM(Control_Unit_write_ram),
    .Read_write_RAM(Control_Unit_read_write_ram));
  Swapper Swapper (
    .Input_1(ram_1_data[3:0]), .Input_2(Swapper_2_output_2), .Control(Control_Unit_load_msb_r),
    .Output_1(Swapper_output_1), .Output_2(Swapper_output_2));
  not not_2 (not_2_out, Control_Unit_write_ram);
  or or_1 (or_1_out, not_1_out, Control_Unit_write_ram);
  Selector Selector (
    .Input_1({Swapper_output_2, Swapper_output_1}), .Control(or_1_out), .Input_2(ram_2_data),
    .Output(Selector_output));
  Swapper Swapper_2 (
    .Input_1(R_q), .Input_2(R_q_2), .Control(Control_Unit_load_msb_r), .Output_2(Swapper_2_output_2));  // open: Output_1
  RAM #(.addrWidth(4)) ram_2 (
    .addr(ram_1_data[3:0]), .data(ram_2_data), .sel(Control_Unit_read_write_ram), .clk(clock_1_out),
    .ld(not_2_out), .clr(counter_1_reset));
  Register R (.D(Selector_output), .Q({R_q_2, R_q}), .clk(clock_1_out), .clr(counter_1_reset));  // open: en
  assign ram_2_data = Control_Unit_write_ram ? {R_q_2, R_q} : 8'bz;  // Controlled_Buffer controlled_buffer_1

  // Notes on the sheet:
  //   Program Memory
  //   Data Memory
endmodule

module Counter (
  input  Clock,
  output [3:0] Output,
  output Reset
);

  wire [3:0] adder_1_out;

  Adder #(.width(4)) adder_1 (.a(4'b0001), .b(Output), .out(adder_1_out), .cout(Reset));  // open: cin
  Register #(.width(4)) register_1 (.D(adder_1_out), .Q(Output), .clk(Clock), .clr(Reset));  // open: en
endmodule

module Swapper (
  input  [3:0] Input_1,
  input  [3:0] Input_2,
  input  Control,
  output [3:0] Output_1,
  output [3:0] Output_2
);

  Multiplexer #(.width(4), .enable("false")) multiplexer_1 (
    .in0(Input_1), .in1(Input_2), .out(Output_1), .sel(Control));
  Multiplexer #(.width(4), .enable("false")) multiplexer_2 (
    .in0(Input_2), .in1(Input_1), .out(Output_2), .sel(Control));
endmodule

module Selector (
  input  [7:0] Input_1,
  input  Control,
  input  [7:0] Input_2,
  output [7:0] Output
);

  wire decoder_1_out0, decoder_1_out1;

  Decoder #(.enable("false")) decoder_1 (.out0(decoder_1_out0), .out1(decoder_1_out1), .sel(Control));
  assign Output = decoder_1_out0 ? Input_1 : 8'bz;  // Controlled_Buffer controlled_buffer_1
  assign Output = decoder_1_out1 ? Input_2 : 8'bz;  // Controlled_Buffer controlled_buffer_2
endmodule

module Control_Unit (
  input  [3:0] Input,
  output Load_msb_lsb_R,
  output Load_msb_R,
  output Write_RAM,
  output Read_write_RAM
);

  wire decoder_1_out8, decoder_1_out10;

  Decoder #(.select(4)) decoder_1 (
    .out8(decoder_1_out8), .out9(Load_msb_R), .out10(decoder_1_out10), .out11(Write_RAM), .sel(Input));  // open: out0, out1, out2, out3, out4, out5, out6, out7, out12, out13, out14, out15, en
  or or_1 (Load_msb_lsb_R, decoder_1_out8, Load_msb_R);
  or or_2 (Read_write_RAM, Write_RAM, decoder_1_out10);
endmodule
